# Fritzing sketch Practica 3 (saved by Fritzing 0.9.3b)
breadboards: 1

parts:
  Componente1 = Arduino Uno (Rev3)
  LED1 = LED - 5mm [color="Red (633nm)" package="5 mm [THT]"]
  U1 = POT [package=pot_mammoth]
  R1 = Resistor [tolerance=±5% resistance=220 package="2512 [SMD]"]

nets:
  N1: Componente1.5V, U1.E
  N2: Componente1.GND, R1.Pin_0
  N3: LED1.cathode, R1.Pin_1
  N4: LED1.anode, U1.A
